// Logisim project ActualFinalGuy.circ as structural Verilog: 18 circuits, main circuit fetchfinal
module fetchfinal (
  input  [11:0] PC,
  input  [7:0] icode_ifun,
  input  [7:0] rArB,
  input  [7:0] byte2,
  input  [7:0] byte3,
  input  [7:0] byte4,
  input  [7:0] byte5,
  input  [7:0] byte6,
  input  [7:0] byte7,
  input  [7:0] byte8,
  input  [7:0] byte9,
  output [11:0] valP,
  output [3:0] icode,
  output [3:0] ifun,
  output [3:0] rA,
  output [3:0] rB,
  output [63:0] valC
);

  wire clock_1_out, clock_2_out, comparator_1_eq, decoder_1_out0, decoder_1_out1, decoder_1_out2,
       decoder_1_out3, decoder_1_out4, decoder_1_out5, decoder_1_out6, decoder_1_out7, decoder_1_out8,
       decoder_1_out9, decoder_1_out10, decoder_1_out11, decoder_1_out12, decoder_1_out13, decoder_1_out14,
       decoder_1_out15, decoder_2_out14, or_1_out, or_2_out, or_3_out, or_4_out, or_5_out;
  wire [3:0] adder_1_out, controlled_buffer_6_out, controlled_buffer_7_out, controlled_buffer_8_out,
       controlled_buffer_9_out, filterra_1_out_3, filterrb_1_out_3, register_1_q;
  wire [11:0] adder_2_out, controlled_buffer_1_out, controlled_buffer_2_out, controlled_buffer_3_out,
       controlled_buffer_4_out, controlled_buffer_5_out;
  wire [63:0] controlled_buffer_10_out, multiplexer_1_out;

  Decoder #(.select(4)) decoder_1 (
    .out0(decoder_1_out0), .out1(decoder_1_out1), .out2(decoder_1_out2), .out3(decoder_1_out3),
    .out4(decoder_1_out4), .out5(decoder_1_out5), .out6(decoder_1_out6), .out7(decoder_1_out7),
    .out8(decoder_1_out8), .out9(decoder_1_out9), .out10(decoder_1_out10), .out11(decoder_1_out11),
    .out12(decoder_1_out12), .out13(decoder_1_out13), .out14(decoder_1_out14), .out15(decoder_1_out15),
    .sel(icode_ifun[7:4]));  // open: en
  or or_1 (or_1_out, decoder_1_out12, decoder_1_out13, decoder_1_out14, decoder_1_out15);
  or or_2 (or_2_out, decoder_1_out0, decoder_1_out1, decoder_1_out9);
  or or_3 (or_3_out, decoder_1_out2, decoder_1_out6, decoder_1_out10, decoder_1_out11);
  or or_4 (or_4_out, decoder_1_out7, decoder_1_out8);
  or or_5 (or_5_out, decoder_1_out3, decoder_1_out4, decoder_1_out5);
  assign controlled_buffer_1_out = or_2_out ? PC : 12'bz;  // Controlled_Buffer controlled_buffer_1
  assign controlled_buffer_2_out = or_3_out ? PC : 12'bz;  // Controlled_Buffer controlled_buffer_2
  assign controlled_buffer_3_out = or_4_out ? PC : 12'bz;  // Controlled_Buffer controlled_buffer_3
  assign controlled_buffer_4_out = or_5_out ? PC : 12'bz;  // Controlled_Buffer controlled_buffer_4
  FilterrA filterra_1 (.icode(icode_ifun[7:4]), .rA(rArB[7:4]), .out_3(filterra_1_out_3));
  FilterrB filterrb_1 (.icode(icode_ifun[7:4]), .rB(rArB[3:0]), .out_3(filterrb_1_out_3));
  Multiplexer #(.width(64)) multiplexer_1 (
    .in0({byte9, byte8, byte7, byte6, byte5, byte4, byte3, byte2}),
    .in1({byte8, byte7, byte6, byte5, byte4, byte3, byte2, rArB}), .out(multiplexer_1_out), .sel(or_4_out));
  Adder #(.width(4)) adder_1 (.a(register_1_q), .b(4'b0001), .out(adder_1_out));  // open: cin, cout
  Decoder #(.select(4)) decoder_2 (
    .out14(decoder_2_out14), .sel(register_1_q));  // open: out0, out1, out2, out3, out4, out5, out6, out7, out8, out9, out10, out11, out12, out13, out15, en
  Adder #(.width(12)) adder_2 (.a(controlled_buffer_1_out), .b(12'h1), .out(adder_2_out));  // open: cin, cout
  Adder #(.width(12)) adder_3 (.a(controlled_buffer_2_out), .b(12'h2), .out(adder_2_out));  // open: cin, cout
  Adder #(.width(12)) adder_4 (.a(controlled_buffer_3_out), .b(12'h9), .out(adder_2_out));  // open: cin, cout
  Adder #(.width(12)) adder_5 (.a(controlled_buffer_4_out), .b(12'ha), .out(adder_2_out));  // open: cin, cout
  Register #(.width(4)) register_1 (
    .D(adder_1_out), .clk(clock_1_out), .Q(register_1_q), .clr(decoder_2_out14));  // open: en
  Clock clock_1 (.out(clock_1_out));
  Comparator #(.width(4)) comparator_1 (.a(4'b1010), .b(register_1_q), .eq(comparator_1_eq));  // open: gt, lt
  assign controlled_buffer_5_out = comparator_1_eq ? adder_2_out : 12'bz;  // Controlled_Buffer controlled_buffer_5
  assign controlled_buffer_6_out = comparator_1_eq ? icode_ifun[7:4] : 4'bz;  // Controlled_Buffer controlled_buffer_6
  assign controlled_buffer_7_out = comparator_1_eq ? icode_ifun[3:0] : 4'bz;  // Controlled_Buffer controlled_buffer_7
  assign controlled_buffer_8_out = comparator_1_eq ? filterra_1_out_3 : 4'bz;  // Controlled_Buffer controlled_buffer_8
  assign controlled_buffer_9_out = comparator_1_eq ? filterrb_1_out_3 : 4'bz;  // Controlled_Buffer controlled_buffer_9
  assign controlled_buffer_10_out = comparator_1_eq ? multiplexer_1_out : 64'bz;  // Controlled_Buffer controlled_buffer_10
  Clock clock_2 (.out(clock_2_out));
  Register #(.width(12)) register_2 (
    .D(controlled_buffer_5_out), .en(comparator_1_eq), .clk(clock_2_out), .Q(valP));  // open: clr
  Register #(.width(4)) register_3 (
    .D(controlled_buffer_6_out), .en(comparator_1_eq), .clk(clock_2_out), .Q(icode));  // open: clr
  Register #(.width(4)) register_4 (
    .D(controlled_buffer_7_out), .en(comparator_1_eq), .clk(clock_2_out), .Q(ifun));  // open: clr
  Register #(.width(4)) register_5 (
    .D(controlled_buffer_8_out), .en(comparator_1_eq), .clk(clock_2_out), .Q(rA));  // open: clr
  Register #(.width(4)) register_6 (
    .D(controlled_buffer_9_out), .en(comparator_1_eq), .clk(clock_2_out), .Q(rB));  // open: clr
  Register #(.width(64)) register_7 (
    .D(controlled_buffer_10_out), .en(comparator_1_eq), .clk(clock_2_out), .Q(valC));  // open: clr

  // Notes on the sheet:
  //   2, 6, A, B: 2 byte
  //   0, 1, 9: 1 byte
  //   7, 8: 9 byte
  //   3, 4, 5: 10 byte
  //   Split
  //   Instruction Failed
  //   Resetter
  //   PassThroughAt10
endmodule

module ALU (
  input  [63:0] aluA,
  input  [63:0] aluB,
  input  [1:0] aluFunIn,
  output O_F,
  output Z_F,
  output S_F,
  output [63:0] valE
);

  wire and_2_out, and_3_out, not_1_out, xor_2_out, xor_3_out;
  wire [63:0] adder_1_out, and_1_out, subtractor_1_out, xor_1_out;

  Adder #(.width(64)) adder_1 (.a(aluA), .b(aluB), .out(adder_1_out));  // open: cin, cout
  Subtractor #(.width(64)) subtractor_1 (.a(aluB), .b(aluA), .out(subtractor_1_out));  // open: bin, bout
  assign and_1_out = aluA & aluB;  // AND_Gate and_1, 64 bits wide
  assign xor_1_out = aluA ^ aluB;  // XOR_Gate xor_1, 64 bits wide
  xor xor_2 (xor_2_out, aluA[63], aluB[63]);
  and and_2 (and_2_out, xor_2_out, not_1_out);
  not not_1 (not_1_out, valE[63]);
  and and_3 (and_3_out, aluA[63], aluB[63]);
  xor xor_3 (xor_3_out, and_3_out, valE[63]);
  Multiplexer #(.select(2), .width(64)) multiplexer_1 (
    .in0(adder_1_out), .in1(subtractor_1_out), .in2(and_1_out), .in3(xor_1_out), .out(valE), .sel(aluFunIn));
  or or_1 (O_F, and_2_out, xor_3_out);
  Comparator #(.width(64)) comparator_1 (.a(valE), .b({64{1'b0}}), .eq(Z_F), .lt(S_F));  // open: gt

  // Notes on the sheet:
  //   aluA: initial=0xffffffffffffffb6
endmodule

module setCC_helper (
  input  [3:0] icode,
  output setCC
);

  Decoder #(.select(4)) decoder_1 (
    .out6(setCC), .sel(icode));  // open: out0, out1, out2, out3, out4, out5, out7, out8, out9, out10, out11, out12, out13, out14, out15, en
endmodule

module FilterrA (
  input  [3:0] icode,
  input  [3:0] rA,
  output [3:0] out_3
);

  wire decoder_1_out2, decoder_1_out4, decoder_1_out5, decoder_1_out6, decoder_1_out10, decoder_1_out11,
       or_1_out;

  Decoder #(.select(4)) decoder_1 (
    .out2(decoder_1_out2), .out4(decoder_1_out4), .out5(decoder_1_out5), .out6(decoder_1_out6),
    .out10(decoder_1_out10), .out11(decoder_1_out11), .sel(icode));  // open: out0, out1, out3, out7, out8, out9, out12, out13, out14, out15, en
  or or_1 (or_1_out, decoder_1_out2, decoder_1_out4, decoder_1_out5, decoder_1_out6, decoder_1_out10, decoder_1_out11);
  Multiplexer #(.width(4)) multiplexer_1 (.in0(4'b1111), .in1(rA), .out(out_3), .sel(or_1_out));
endmodule

module FilterrB (
  input  [3:0] icode,
  input  [3:0] rB,
  output [3:0] out_3
);

  wire decoder_1_out2, decoder_1_out3, decoder_1_out4, decoder_1_out5, decoder_1_out6, or_1_out;

  Decoder #(.select(4)) decoder_1 (
    .out2(decoder_1_out2), .out3(decoder_1_out3), .out4(decoder_1_out4), .out5(decoder_1_out5),
    .out6(decoder_1_out6), .sel(icode));  // open: out0, out1, out7, out8, out9, out10, out11, out12, out13, out14, out15, en
  or or_1 (or_1_out, decoder_1_out2, decoder_1_out3, decoder_1_out4, decoder_1_out5, decoder_1_out6);
  Multiplexer #(.width(4)) multiplexer_1 (.in0(4'b1111), .in1(rB), .out(out_3), .sel(or_1_out));
endmodule

module FetchAlign (
  input  [3:0] icode,
  input  [7:0] rArB,
  input  [7:0] valC,
  input  [7:0] in_4,
  input  [7:0] in_5,
  input  [7:0] in_6,
  input  [7:0] in_7,
  input  [7:0] in_8,
  input  [7:0] in_9,
  input  [7:0] in_10,
  output [3:0] rAout,
  output [3:0] rBout,
  output [7:0] valCout,
  output [7:0] out_14,
  output [7:0] out_15,
  output [7:0] out_16,
  output [7:0] out_17,
  output [7:0] out_18,
  output [7:0] out_19,
  output [7:0] out_20
);

  FilterrA filterra_1 (.icode(icode), .rA(rArB[7:4]), .out_3(rAout));
  FilterrB filterrb_1 (.icode(icode), .rB(rArB[3:0]), .out_3(rBout));

  assign out_14 = in_4;
  assign out_15 = in_5;
  assign out_16 = in_6;
  assign out_17 = in_7;
  assign out_18 = in_8;
  assign out_19 = in_9;
  assign out_20 = in_10;
  assign valCout = valC;
endmodule

module cond (
  input  SF,
  input  ZF,
  input  OFlag,
  input  [3:0] ifun,
  output Cnd
);

  wire and_1_out, and_2_out, and_3_out, and_4_out, and_5_out, and_6_out, and_7_out, and_8_out,
       decoder_1_out0, decoder_1_out1, decoder_1_out2, decoder_1_out3, decoder_1_out4, decoder_1_out5,
       decoder_1_out6, not_1_out, not_2_out, or_1_out;

  Decoder #(.select(4)) decoder_1 (
    .out0(decoder_1_out0), .out1(decoder_1_out1), .out2(decoder_1_out2), .out3(decoder_1_out3),
    .out4(decoder_1_out4), .out5(decoder_1_out5), .out6(decoder_1_out6), .sel(ifun));  // open: out7, out8, out9, out10, out11, out12, out13, out14, out15, en
  not not_1 (not_1_out, and_6_out);
  and and_1 (and_1_out, not_1_out, not_2_out);
  and and_2 (and_2_out, and_1_out, decoder_1_out6);
  not not_2 (not_2_out, ZF);
  and and_3 (and_3_out, ZF, decoder_1_out3);
  and and_4 (and_4_out, not_2_out, decoder_1_out4);
  and and_5 (and_5_out, not_1_out, decoder_1_out5);
  or or_1 (or_1_out, ZF, and_6_out);
  and and_6 (and_6_out, SF, OFlag);
  and and_7 (and_7_out, and_6_out, decoder_1_out2);
  and and_8 (and_8_out, or_1_out, decoder_1_out1);
  or or_2 (Cnd, decoder_1_out0, and_8_out, and_7_out, and_3_out, and_4_out, and_5_out, and_2_out);
endmodule

module register_file_but_cool (
  input  [63:0] valM,
  input  [63:0] valE,
  input  [3:0] dstE,
  input  [3:0] dstM,
  input  [3:0] srcA,
  input  [3:0] srcB,
  output [63:0] valA,
  output [63:0] valB
);

  wire clock_1_out, clock_2_out, comparator_1_eq, comparator_2_eq, comparator_3_eq, decoder_1_out14, or_1_out;
  wire [3:0] adder_1_out, register_2_q;
  wire [63:0] register_1_q;

  Clock clock_1 (.out(clock_1_out));
  Register #(.width(64)) register_1 (.D(valE), .en(or_1_out), .clk(clock_1_out), .Q(register_1_q));  // open: clr
  Register #(.width(4)) register_2 (
    .D(adder_1_out), .clk(clock_2_out), .Q(register_2_q), .clr(decoder_1_out14));  // open: en
  Adder #(.width(4)) adder_1 (.a(register_2_q), .b(4'b0001), .out(adder_1_out));  // open: cin, cout
  Clock clock_2 (.out(clock_2_out));
  Decoder #(.select(4)) decoder_1 (
    .out14(decoder_1_out14), .sel(register_2_q));  // open: out0, out1, out2, out3, out4, out5, out6, out7, out8, out9, out10, out11, out12, out13, out15, en
  register_file register_file_1 (
    .clk(clock_1_out), .M(valM), .E(register_1_q), .dstE(dstE), .dstM(dstM), .srcA(srcA), .srcB(srcB),
    .A(valA), .B(valB));
  Comparator #(.width(4)) comparator_1 (.a(4'b1011), .b(register_2_q), .eq(comparator_1_eq));  // open: gt, lt
  Comparator #(.width(4)) comparator_2 (.a(4'b1010), .b(register_2_q), .eq(comparator_2_eq));  // open: gt, lt
  Comparator #(.width(4)) comparator_3 (.a(4'b1100), .b(register_2_q), .eq(comparator_3_eq));  // open: gt, lt
  Register register_3 ();  // open: D, en, clk, Q, clr
  buf or_1 (or_1_out, comparator_1_eq);  // OR_Gate
endmodule

module register_file (
  input  clk,
  input  [63:0] M,
  input  [63:0] E,
  input  [3:0] dstE,
  input  [3:0] dstM,
  input  [3:0] srcA,
  input  [3:0] srcB,
  output [63:0] A,
  output [63:0] B
);

  wire decoder_1_out0, decoder_1_out1, decoder_1_out2, decoder_1_out3, decoder_1_out4, decoder_1_out5,
       decoder_1_out6, decoder_1_out7, decoder_1_out8, decoder_1_out9, decoder_1_out10, decoder_1_out11,
       decoder_1_out12, decoder_1_out13, decoder_1_out14, decoder_2_out0, decoder_2_out1, decoder_2_out2,
       decoder_2_out3, decoder_2_out4, decoder_2_out5, decoder_2_out6, decoder_2_out7, decoder_2_out8,
       decoder_2_out9, decoder_2_out10, decoder_2_out11, decoder_2_out12, decoder_2_out13, decoder_2_out14,
       decoder_3_out0, decoder_3_out1, decoder_3_out2, decoder_3_out3, decoder_3_out4, decoder_3_out5,
       decoder_3_out6, decoder_3_out7, decoder_3_out8, decoder_3_out9, decoder_3_out10, decoder_3_out11,
       decoder_3_out12, decoder_3_out13, decoder_3_out14, decoder_4_out0, decoder_4_out1, decoder_4_out2,
       decoder_4_out3, decoder_4_out4, decoder_4_out5, decoder_4_out6, decoder_4_out7, decoder_4_out8,
       decoder_4_out9, decoder_4_out10, decoder_4_out11, decoder_4_out12, decoder_4_out13, decoder_4_out14,
       or_1_out, or_2_out, or_3_out, or_4_out, or_5_out, or_6_out, or_7_out, or_8_out, or_9_out, or_10_out,
       or_11_out, or_12_out, or_13_out, or_14_out, or_15_out;
  wire [63:0] multiplexer_1_out, multiplexer_2_out, multiplexer_3_out, multiplexer_4_out, multiplexer_5_out,
       multiplexer_6_out, multiplexer_7_out, multiplexer_8_out, multiplexer_9_out, multiplexer_10_out,
       multiplexer_11_out, multiplexer_12_out, multiplexer_13_out, multiplexer_14_out, multiplexer_15_out,
       register_1_q, register_2_q, register_3_q, register_4_q, register_5_q, register_6_q, register_7_q,
       register_8_q, register_9_q, register_10_q, register_11_q, register_12_q, register_13_q, register_14_q,
       register_15_q;

  Decoder #(.select(4)) decoder_1 (
    .out0(decoder_1_out0), .out1(decoder_1_out1), .out2(decoder_1_out2), .out3(decoder_1_out3),
    .out4(decoder_1_out4), .out5(decoder_1_out5), .out6(decoder_1_out6), .out7(decoder_1_out7),
    .out8(decoder_1_out8), .out9(decoder_1_out9), .out10(decoder_1_out10), .out11(decoder_1_out11),
    .out12(decoder_1_out12), .out13(decoder_1_out13), .out14(decoder_1_out14), .sel(dstM));  // open: out15, en
  Decoder #(.select(4)) decoder_2 (
    .out0(decoder_2_out0), .out1(decoder_2_out1), .out2(decoder_2_out2), .out3(decoder_2_out3),
    .out4(decoder_2_out4), .out5(decoder_2_out5), .out6(decoder_2_out6), .out7(decoder_2_out7),
    .out8(decoder_2_out8), .out9(decoder_2_out9), .out10(decoder_2_out10), .out11(decoder_2_out11),
    .out12(decoder_2_out12), .out13(decoder_2_out13), .out14(decoder_2_out14), .sel(dstE));  // open: out15, en
  Multiplexer #(.width(64)) multiplexer_1 (.in0(M), .in1(E), .out(multiplexer_1_out), .sel(decoder_2_out0));
  Multiplexer #(.width(64)) multiplexer_2 (.in0(M), .in1(E), .out(multiplexer_2_out), .sel(decoder_2_out1));
  Multiplexer #(.width(64)) multiplexer_3 (.in0(M), .in1(E), .out(multiplexer_3_out), .sel(decoder_2_out2));
  Multiplexer #(.width(64)) multiplexer_4 (.in0(M), .in1(E), .out(multiplexer_4_out), .sel(decoder_2_out3));
  Multiplexer #(.width(64)) multiplexer_5 (.in0(M), .in1(E), .out(multiplexer_5_out), .sel(decoder_2_out4));
  Multiplexer #(.width(64)) multiplexer_6 (.in0(M), .in1(E), .out(multiplexer_6_out), .sel(decoder_2_out5));
  Multiplexer #(.width(64)) multiplexer_7 (.in0(M), .in1(E), .out(multiplexer_7_out), .sel(decoder_2_out6));
  Multiplexer #(.width(64)) multiplexer_8 (.in0(M), .in1(E), .out(multiplexer_8_out), .sel(decoder_2_out7));
  Multiplexer #(.width(64)) multiplexer_9 (.in0(M), .in1(E), .out(multiplexer_9_out), .sel(decoder_2_out8));
  Multiplexer #(.width(64)) multiplexer_10 (.in0(M), .in1(E), .out(multiplexer_10_out), .sel(decoder_2_out9));
  Multiplexer #(.width(64)) multiplexer_11 (.in0(M), .in1(E), .out(multiplexer_11_out), .sel(decoder_2_out10));
  Multiplexer #(.width(64)) multiplexer_12 (.in0(M), .in1(E), .out(multiplexer_12_out), .sel(decoder_2_out11));
  Multiplexer #(.width(64)) multiplexer_13 (.in0(M), .in1(E), .out(multiplexer_13_out), .sel(decoder_2_out12));
  Multiplexer #(.width(64)) multiplexer_14 (.in0(M), .in1(E), .out(multiplexer_14_out), .sel(decoder_2_out13));
  Multiplexer #(.width(64)) multiplexer_15 (.in0(M), .in1(E), .out(multiplexer_15_out), .sel(decoder_2_out14));
  Register #(.width(64)) register_1 (.D(multiplexer_1_out), .en(or_1_out), .clk(clk), .Q(register_1_q));  // open: clr
  or or_1 (or_1_out, decoder_2_out0, decoder_1_out0);
  Register #(.width(64)) register_2 (.D(multiplexer_2_out), .en(or_2_out), .clk(clk), .Q(register_2_q));  // open: clr
  or or_2 (or_2_out, decoder_2_out1, decoder_1_out1);
  Register #(.width(64)) register_3 (.D(multiplexer_3_out), .en(or_3_out), .clk(clk), .Q(register_3_q));  // open: clr
  or or_3 (or_3_out, decoder_2_out2, decoder_1_out2);
  Register #(.width(64)) register_4 (.D(multiplexer_4_out), .en(or_4_out), .clk(clk), .Q(register_4_q));  // open: clr
  or or_4 (or_4_out, decoder_2_out3, decoder_1_out3);
  Register #(.width(64)) register_5 (.D(multiplexer_5_out), .en(or_5_out), .clk(clk), .Q(register_5_q));  // open: clr
  or or_5 (or_5_out, decoder_2_out4, decoder_1_out4);
  Register #(.width(64)) register_6 (.D(multiplexer_6_out), .en(or_6_out), .clk(clk), .Q(register_6_q));  // open: clr
  or or_6 (or_6_out, decoder_2_out5, decoder_1_out5);
  Register #(.width(64)) register_7 (.D(multiplexer_7_out), .en(or_7_out), .clk(clk), .Q(register_7_q));  // open: clr
  or or_7 (or_7_out, decoder_2_out6, decoder_1_out6);
  Register #(.width(64)) register_8 (.D(multiplexer_8_out), .en(or_8_out), .clk(clk), .Q(register_8_q));  // open: clr
  or or_8 (or_8_out, decoder_2_out7, decoder_1_out7);
  Register #(.width(64)) register_9 (.D(multiplexer_9_out), .en(or_9_out), .clk(clk), .Q(register_9_q));  // open: clr
  or or_9 (or_9_out, decoder_2_out8, decoder_1_out8);
  Register #(.width(64)) register_10 (
    .D(multiplexer_10_out), .en(or_10_out), .clk(clk), .Q(register_10_q));  // open: clr
  or or_10 (or_10_out, decoder_2_out9, decoder_1_out9);
  Register #(.width(64)) register_11 (
    .D(multiplexer_11_out), .en(or_11_out), .clk(clk), .Q(register_11_q));  // open: clr
  or or_11 (or_11_out, decoder_2_out10, decoder_1_out10);
  Register #(.width(64)) register_12 (
    .D(multiplexer_12_out), .en(or_12_out), .clk(clk), .Q(register_12_q));  // open: clr
  or or_12 (or_12_out, decoder_2_out11, decoder_1_out11);
  Register #(.width(64)) register_13 (
    .D(multiplexer_13_out), .en(or_13_out), .clk(clk), .Q(register_13_q));  // open: clr
  or or_13 (or_13_out, decoder_2_out12, decoder_1_out12);
  Register #(.width(64)) register_14 (
    .D(multiplexer_14_out), .en(or_14_out), .clk(clk), .Q(register_14_q));  // open: clr
  or or_14 (or_14_out, decoder_2_out13, decoder_1_out13);
  Register #(.width(64)) register_15 (
    .D(multiplexer_15_out), .en(or_15_out), .clk(clk), .Q(register_15_q));  // open: clr
  or or_15 (or_15_out, decoder_2_out14, decoder_1_out14);
  assign A = decoder_3_out0 ? register_1_q : 64'bz;  // Controlled_Buffer controlled_buffer_1
  assign B = decoder_4_out0 ? register_1_q : 64'bz;  // Controlled_Buffer controlled_buffer_2
  assign A = decoder_3_out1 ? register_2_q : 64'bz;  // Controlled_Buffer controlled_buffer_3
  assign B = decoder_4_out1 ? register_2_q : 64'bz;  // Controlled_Buffer controlled_buffer_4
  assign A = decoder_3_out2 ? register_3_q : 64'bz;  // Controlled_Buffer controlled_buffer_5
  assign B = decoder_4_out2 ? register_3_q : 64'bz;  // Controlled_Buffer controlled_buffer_6
  assign A = decoder_3_out3 ? register_4_q : 64'bz;  // Controlled_Buffer controlled_buffer_7
  assign B = decoder_4_out3 ? register_4_q : 64'bz;  // Controlled_Buffer controlled_buffer_8
  assign A = decoder_3_out4 ? register_5_q : 64'bz;  // Controlled_Buffer controlled_buffer_9
  assign B = decoder_4_out4 ? register_5_q : 64'bz;  // Controlled_Buffer controlled_buffer_10
  assign A = decoder_3_out5 ? register_6_q : 64'bz;  // Controlled_Buffer controlled_buffer_11
  assign B = decoder_4_out5 ? register_6_q : 64'bz;  // Controlled_Buffer controlled_buffer_12
  assign A = decoder_3_out6 ? register_7_q : 64'bz;  // Controlled_Buffer controlled_buffer_13
  assign B = decoder_4_out6 ? register_7_q : 64'bz;  // Controlled_Buffer controlled_buffer_14
  assign A = decoder_3_out7 ? register_8_q : 64'bz;  // Controlled_Buffer controlled_buffer_15
  assign B = decoder_4_out7 ? register_8_q : 64'bz;  // Controlled_Buffer controlled_buffer_16
  assign A = decoder_3_out8 ? register_9_q : 64'bz;  // Controlled_Buffer controlled_buffer_17
  assign B = decoder_4_out8 ? register_9_q : 64'bz;  // Controlled_Buffer controlled_buffer_18
  assign A = decoder_3_out9 ? register_10_q : 64'bz;  // Controlled_Buffer controlled_buffer_19
  assign B = decoder_4_out9 ? register_10_q : 64'bz;  // Controlled_Buffer controlled_buffer_20
  assign A = decoder_3_out10 ? register_11_q : 64'bz;  // Controlled_Buffer controlled_buffer_21
  assign B = decoder_4_out10 ? register_11_q : 64'bz;  // Controlled_Buffer controlled_buffer_22
  assign A = decoder_3_out11 ? register_12_q : 64'bz;  // Controlled_Buffer controlled_buffer_23
  assign B = decoder_4_out11 ? register_12_q : 64'bz;  // Controlled_Buffer controlled_buffer_24
  assign A = decoder_3_out12 ? register_13_q : 64'bz;  // Controlled_Buffer controlled_buffer_25
  assign B = decoder_4_out12 ? register_13_q : 64'bz;  // Controlled_Buffer controlled_buffer_26
  assign A = decoder_3_out13 ? register_14_q : 64'bz;  // Controlled_Buffer controlled_buffer_27
  assign B = decoder_4_out13 ? register_14_q : 64'bz;  // Controlled_Buffer controlled_buffer_28
  assign A = decoder_3_out14 ? register_15_q : 64'bz;  // Controlled_Buffer controlled_buffer_29
  assign B = decoder_4_out14 ? register_15_q : 64'bz;  // Controlled_Buffer controlled_buffer_30
  Decoder #(.select(4)) decoder_3 (
    .out0(decoder_3_out0), .out1(decoder_3_out1), .out2(decoder_3_out2), .out3(decoder_3_out3),
    .out4(decoder_3_out4), .out5(decoder_3_out5), .out6(decoder_3_out6), .out7(decoder_3_out7),
    .out8(decoder_3_out8), .out9(decoder_3_out9), .out10(decoder_3_out10), .out11(decoder_3_out11),
    .out12(decoder_3_out12), .out13(decoder_3_out13), .out14(decoder_3_out14), .sel(srcA), .en(1'b1));  // open: out15
  Decoder #(.select(4)) decoder_4 (
    .out0(decoder_4_out0), .out1(decoder_4_out1), .out2(decoder_4_out2), .out3(decoder_4_out3),
    .out4(decoder_4_out4), .out5(decoder_4_out5), .out6(decoder_4_out6), .out7(decoder_4_out7),
    .out8(decoder_4_out8), .out9(decoder_4_out9), .out10(decoder_4_out10), .out11(decoder_4_out11),
    .out12(decoder_4_out12), .out13(decoder_4_out13), .out14(decoder_4_out14), .sel(srcB), .en(1'b1));  // open: out15
endmodule

module setCC (
  input  O_F_in,
  input  Z_F_in,
  input  S_F_in,
  input  set,
  output O_F,
  output Z_F,
  output S_F
);

  wire clock_1_out, clock_2_out, comparator_1_eq, decoder_1_out14;
  wire [3:0] adder_1_out, register_1_q;

  Clock clock_1 (.out(clock_1_out));
  Register #(.width(4)) register_1 (
    .D(adder_1_out), .clk(clock_2_out), .Q(register_1_q), .clr(decoder_1_out14));  // open: en
  Adder #(.width(4)) adder_1 (.a(register_1_q), .b(4'b0001), .out(adder_1_out));  // open: cin, cout
  Clock clock_2 (.out(clock_2_out));
  Decoder #(.select(4)) decoder_1 (
    .out14(decoder_1_out14), .sel(register_1_q));  // open: out0, out1, out2, out3, out4, out5, out6, out7, out8, out9, out10, out11, out12, out13, out15, en
  Register #(.width(1)) register_2 (.D(O_F_in), .en(set), .clk(clock_1_out), .Q(O_F));  // open: clr
  Register #(.width(1)) register_3 (.D(Z_F_in), .en(set), .clk(clock_1_out), .Q(Z_F));  // open: clr
  Register #(.width(1)) register_4 (.D(S_F_in), .en(set), .clk(clock_1_out), .Q(S_F));  // open: clr
  Comparator #(.width(4)) comparator_1 (.a(4'b1010), .b(register_1_q), .eq(comparator_1_eq));  // open: gt, lt
endmodule

module srcDest (
  input  [3:0] rA,
  input  [3:0] icode,
  input  [3:0] rB,
  output [3:0] dstE,
  output [3:0] dstM,
  output [3:0] srcA,
  output [3:0] srcB
);

  wire and_1_out, and_2_out, and_3_out, and_4_out, and_5_out, and_6_out, and_7_out, or_1_out, or_2_out;
  wire [3:0] multiplexer_1_out, multiplexer_2_out, multiplexer_3_out;

  or or_1 (or_1_out, icode[1], icode[2]);
  and and_1 (and_1_out, icode[0], ~icode[1], icode[2], ~icode[3]);  // AND_Gate
  and and_2 (and_2_out, ~icode[0], or_1_out, ~icode[3]);  // AND_Gate
  and and_3 (and_3_out, ~icode[0], icode[1], ~icode[2], icode[3]);  // AND_Gate
  and and_4 (and_4_out, icode[0], ~icode[2], icode[3]);  // AND_Gate
  and and_5 (and_5_out, ~icode[2], icode[3]);  // AND_Gate
  and and_6 (and_6_out, ~icode[1], icode[2], ~icode[3]);  // AND_Gate
  and and_7 (and_7_out, icode[1], ~icode[2], ~icode[3]);  // AND_Gate
  or or_2 (or_2_out, and_2_out, and_3_out);
  Multiplexer #(.width(4)) multiplexer_1 (.in0(rB), .in1(4'b1111), .out(multiplexer_1_out), .sel(and_6_out));
  Multiplexer #(.width(4)) multiplexer_2 (.in0(rB), .in1(4'b1111), .out(multiplexer_2_out), .sel(and_7_out));
  Multiplexer #(.width(4)) multiplexer_3 (.in0(rA), .in1(4'b1111), .out(multiplexer_3_out), .sel(and_1_out));
  Multiplexer #(.width(4)) multiplexer_4 (.in0(rA), .in1(4'b1111), .out(dstM), .sel(or_2_out));
  Multiplexer #(.width(4)) multiplexer_5 (.in0(multiplexer_2_out), .in1(4'b0100), .out(srcB), .sel(and_5_out));
  Multiplexer #(.width(4)) multiplexer_6 (.in0(multiplexer_3_out), .out(srcA), .sel(and_4_out));  // open: in1
  Multiplexer #(.width(4)) multiplexer_7 (.in0(multiplexer_1_out), .in1(4'b0100), .out(dstE), .sel(and_5_out));

  // Notes on the sheet:
  //   9B
  //   89AB
  //   5 B
  //   4 5 6
  //   89AB
  //   2 4 6 A
  //   2 3 6 
  //   89AB
  //   RSP:9 B
endmodule

module ALUFun (
  input  [3:0] iCode,
  input  [3:0] iFun,
  output [1:0] ALUFunOut
);

  wire Add_out, decoder_1_out0, decoder_1_out1, decoder_1_out2, decoder_1_out3, decoder_1_out4,
       decoder_1_out5, decoder_1_out6, decoder_1_out7, decoder_1_out8, decoder_1_out9, decoder_1_out10,
       decoder_1_out11, decoder_2_out0, decoder_2_out1, decoder_2_out2, decoder_2_out3;

  Decoder #(.select(4)) decoder_1 (
    .out0(decoder_1_out0), .out1(decoder_1_out1), .out2(decoder_1_out2), .out3(decoder_1_out3),
    .out4(decoder_1_out4), .out5(decoder_1_out5), .out6(decoder_1_out6), .out7(decoder_1_out7),
    .out8(decoder_1_out8), .out9(decoder_1_out9), .out10(decoder_1_out10), .out11(decoder_1_out11),
    .sel(iCode));  // open: out12, out13, out14, out15, en
  Decoder #(.select(2)) decoder_2 (
    .out0(decoder_2_out0), .out1(decoder_2_out1), .out2(decoder_2_out2), .out3(decoder_2_out3),
    .sel(iFun[1:0]), .en(decoder_1_out6));
  or Add (Add_out, decoder_1_out0, decoder_1_out1, decoder_1_out2, decoder_1_out3, decoder_1_out4, decoder_1_out5, decoder_1_out7, decoder_1_out8, decoder_1_out9, decoder_1_out10, decoder_1_out11, decoder_2_out0);
  assign ALUFunOut = Add_out ? 2'b00 : 2'bz;  // Controlled_Buffer controlled_buffer_1
  assign ALUFunOut = decoder_2_out1 ? 2'b01 : 2'bz;  // Controlled_Buffer controlled_buffer_2
  assign ALUFunOut = decoder_2_out2 ? 2'b10 : 2'bz;  // Controlled_Buffer controlled_buffer_3
  assign ALUFunOut = decoder_2_out3 ? 2'b11 : 2'bz;  // Controlled_Buffer controlled_buffer_4

  // Notes on the sheet:
  //   OP
endmodule

module ALUB (
  input  [63:0] ValB,
  input  [3:0] iCode,
  output [63:0] ALUBOut
);

  Multiplexer #(.select(4), .width(64)) multiplexer_1 (
    .in0({64{1'b0}}), .in1({64{1'b0}}), .in2({64{1'b0}}), .in3({64{1'b0}}), .in4({64{1'b0}}),
    .in5({64{1'b0}}), .in6(ValB), .in7({64{1'b0}}), .in8({64{1'b0}}), .in9({64{1'b0}}), .in10({64{1'b0}}),
    .in11({64{1'b0}}), .in12({64{1'b0}}), .in13({64{1'b0}}), .in14({64{1'b0}}), .in15({64{1'b0}}),
    .out(ALUBOut), .sel(iCode));
endmodule

module ALUA (
  input  [63:0] ValA,
  input  [63:0] ValC,
  input  [3:0] iCode,
  output [63:0] ALUAOut
);

  Multiplexer #(.select(4), .width(64)) multiplexer_1 (
    .in2(ValA), .in3(ValC), .in4(ValC), .in5(ValC), .in6(ValA), .in10(64'h8), .in11(64'hfffffffffffffff8),
    .out(ALUAOut), .sel(iCode));  // open: in0, in1, in7, in8, in9, in12, in13, in14, in15
endmodule

module newPC (
  input  [11:0] ValP,
  input  [3:0] icode,
  input  [63:0] ValC,
  input  Cnd,
  input  [63:0] ValM,
  output [11:0] PC
);

  wire and_1_out, decoder_1_out0, decoder_1_out1, decoder_1_out2, decoder_1_out3, decoder_1_out4,
       decoder_1_out5, decoder_1_out6, decoder_1_out7, not_1_out, or_1_out;
  wire [11:0] multiplexer_1_out;

  Decoder #(.select(4)) decoder_1 (
    .out0(decoder_1_out0), .out1(decoder_1_out1), .out2(decoder_1_out2), .out3(decoder_1_out3),
    .out4(decoder_1_out4), .out5(decoder_1_out5), .out6(decoder_1_out6), .out7(decoder_1_out7), .sel(icode));  // open: out8, out9, out10, out11, out12, out13, out14, out15, en
  or or_1 (or_1_out, decoder_1_out0, decoder_1_out1, decoder_1_out2, decoder_1_out3, decoder_1_out4, decoder_1_out5, decoder_1_out6);
  and and_1 (and_1_out, decoder_1_out7, Cnd);
  not not_1 (not_1_out, or_1_out);
  Multiplexer #(.width(12)) multiplexer_1 (.in0(ValP), .in1(ValC[11:0]), .out(multiplexer_1_out), .sel(and_1_out));
  assign PC = or_1_out ? ValP : 12'bz;  // Controlled_Buffer controlled_buffer_1
  assign PC = not_1_out ? multiplexer_1_out : 12'bz;  // Controlled_Buffer controlled_buffer_2
endmodule

module main (
);

  wire alu_1_o_f, alu_1_s_f, alu_1_z_f, CC_o_f, CC_s_f, CC_z_f, clock_1_out, clock_2_out, clock_3_out,
       clock_5_out, clock_6_out, clock_7_out, comparator_1_eq, comparator_2_eq, comparator_3_eq, cond_1_cnd,
       decoder_1_out14, decoder_2_out14, not_1_out, SET_CC_setcc;
  wire [1:0] alufun_1_alufunout;
  wire [3:0] adder_1_out, adder_2_out, fetchfinal_1_icode, fetchfinal_1_ifun, fetchfinal_1_ra,
       fetchfinal_1_rb, register_2_q, register_3_q, srcdest_1_dste, srcdest_1_dstm, srcdest_1_srca,
       srcdest_1_srcb;
  wire [7:0] intmem2_1_byte0, intmem2_1_byte1, intmem2_1_byte2, intmem2_1_byte3, intmem2_1_byte4,
       intmem2_1_byte5, intmem2_1_byte6, intmem2_1_byte7, intmem2_1_byte8, intmem2_1_byte9;
  wire [11:0] fetchfinal_1_valp, newpc_1_pc, register_1_q;
  wire [63:0] alu_1_vale, alua_1_aluaout, alub_1_alubout, controlled_buffer_1_out, fetchfinal_1_valc,
       memory_unit_1_valm, register_4_q, register_file_but_cool_1_vala, register_file_but_cool_1_valb;

  Comparator #(.width(4)) comparator_1 (.a(fetchfinal_1_icode), .b(4'b0000), .eq(comparator_1_eq));  // open: gt, lt
  Register #(.width(12)) register_1 (.D(newpc_1_pc), .en(not_1_out), .clk(clock_1_out), .Q(register_1_q));  // open: clr
  not not_1 (not_1_out, comparator_1_eq);
  Clock clock_1 (.out(clock_1_out));
  Clock clock_2 (.out(clock_2_out));
  intmem2 intmem2_1 (
    .PC(register_1_q), .clock(clock_2_out), .byte0(intmem2_1_byte0), .byte1(intmem2_1_byte1),
    .byte2(intmem2_1_byte2), .byte3(intmem2_1_byte3), .byte4(intmem2_1_byte4), .byte5(intmem2_1_byte5),
    .byte6(intmem2_1_byte6), .byte7(intmem2_1_byte7), .byte8(intmem2_1_byte8), .byte9(intmem2_1_byte9));
  fetchfinal fetchfinal_1 (
    .PC(register_1_q), .icode_ifun(intmem2_1_byte0), .rArB(intmem2_1_byte1), .byte2(intmem2_1_byte2),
    .byte3(intmem2_1_byte3), .byte4(intmem2_1_byte4), .byte5(intmem2_1_byte5), .byte6(intmem2_1_byte6),
    .byte7(intmem2_1_byte7), .byte8(intmem2_1_byte8), .byte9(intmem2_1_byte9), .valP(fetchfinal_1_valp),
    .icode(fetchfinal_1_icode), .ifun(fetchfinal_1_ifun), .rA(fetchfinal_1_ra), .rB(fetchfinal_1_rb),
    .valC(fetchfinal_1_valc));
  srcDest srcdest_1 (
    .rA(fetchfinal_1_ra), .icode(fetchfinal_1_icode), .rB(fetchfinal_1_rb), .dstE(srcdest_1_dste),
    .dstM(srcdest_1_dstm), .srcA(srcdest_1_srca), .srcB(srcdest_1_srcb));
  register_file_but_cool register_file_but_cool_1 (
    .valM(memory_unit_1_valm), .valE(alu_1_vale), .dstE(srcdest_1_dste), .dstM(srcdest_1_dstm),
    .srcA(srcdest_1_srca), .srcB(srcdest_1_srcb), .valA(register_file_but_cool_1_vala),
    .valB(register_file_but_cool_1_valb));
  Register #(.width(4)) register_2 (
    .D(adder_1_out), .clk(clock_3_out), .Q(register_2_q), .clr(decoder_1_out14));  // open: en
  Adder #(.width(4)) adder_1 (.a(register_2_q), .b(4'b0001), .out(adder_1_out));  // open: cin, cout
  Clock clock_3 (.out(clock_3_out));
  Decoder #(.select(4)) decoder_1 (
    .out14(decoder_1_out14), .sel(register_2_q));  // open: out0, out1, out2, out3, out4, out5, out6, out7, out8, out9, out10, out11, out12, out13, out15, en
  ALUA alua_1 (
    .ValA(register_file_but_cool_1_vala), .ValC(fetchfinal_1_valc), .iCode(fetchfinal_1_icode),
    .ALUAOut(alua_1_aluaout));
  ALUB alub_1 (.ValB(register_file_but_cool_1_valb), .iCode(fetchfinal_1_icode), .ALUBOut(alub_1_alubout));
  Comparator #(.width(4)) comparator_2 (.a(4'b1101), .b(register_2_q), .eq(comparator_2_eq));  // open: gt, lt
  Clock clock_4 ();  // open: out
  ALUFun alufun_1 (.iCode(fetchfinal_1_icode), .iFun(fetchfinal_1_ifun), .ALUFunOut(alufun_1_alufunout));
  ALU alu_1 (
    .aluA(alua_1_aluaout), .aluB(alub_1_alubout), .aluFunIn(alufun_1_alufunout), .O_F(alu_1_o_f),
    .Z_F(alu_1_z_f), .S_F(alu_1_s_f), .valE(alu_1_vale));
  setCC_helper SET_CC (.icode(fetchfinal_1_icode), .setCC(SET_CC_setcc));
  Register #(.width(4)) register_3 (
    .D(adder_2_out), .clk(clock_5_out), .Q(register_3_q), .clr(decoder_2_out14));  // open: en
  Adder #(.width(4)) adder_2 (.a(register_3_q), .b(4'b0001), .out(adder_2_out));  // open: cin, cout
  Clock clock_5 (.out(clock_5_out));
  Decoder #(.select(4)) decoder_2 (
    .out14(decoder_2_out14), .sel(register_3_q));  // open: out0, out1, out2, out3, out4, out5, out6, out7, out8, out9, out10, out11, out12, out13, out15, en
  setCC CC (
    .O_F_in(alu_1_o_f), .Z_F_in(alu_1_z_f), .S_F_in(alu_1_s_f), .set(SET_CC_setcc), .O_F(CC_o_f),
    .Z_F(CC_z_f), .S_F(CC_s_f));
  Comparator #(.width(4)) comparator_3 (.a(4'b1100), .b(register_3_q), .eq(comparator_3_eq));  // open: gt, lt
  Register #(.width(64)) register_4 (
    .D(controlled_buffer_1_out), .en(comparator_3_eq), .clk(clock_6_out), .Q(register_4_q));  // open: clr
  Clock clock_6 (.out(clock_6_out));
  assign controlled_buffer_1_out = comparator_3_eq ? alu_1_vale : 64'bz;  // Controlled_Buffer controlled_buffer_1
  cond cond_1 (.SF(CC_s_f), .ZF(CC_z_f), .OFlag(CC_o_f), .ifun(fetchfinal_1_ifun), .Cnd(cond_1_cnd));
  Clock clock_7 (.out(clock_7_out));
  memory_unit memory_unit_1 (
    .valE(register_4_q), .valA(register_file_but_cool_1_vala), .valP({{52{1'b0}}, fetchfinal_1_valp}),
    .clk(clock_7_out), .icode(fetchfinal_1_icode), .valM(memory_unit_1_valm));
  newPC newpc_1 (
    .ValP(fetchfinal_1_valp), .icode(fetchfinal_1_icode), .ValC(fetchfinal_1_valc), .Cnd(cond_1_cnd),
    .ValM(memory_unit_1_valm), .PC(newpc_1_pc));

  // Notes on the sheet:
  //   10 cycle
  //   FETCH
  //   1 cycle
  //   icode/ifun
  //   ValC
  //   DECODE
  //   1 cycle question mark
  //   Prevent Skipped Mem Writeback
  //   WriteBack
  //   EXECUTE
  //   Prevent Skipped Mem WriteTo
  //   1 cycle
  //   MEMORY
  //   1 cycle
  //   NEWPC
endmodule

module memory_unit (
  input  [63:0] valE,
  input  [63:0] valA,
  input  [63:0] valP,
  input  clk,
  input  [3:0] icode,
  output [63:0] valM
);

  wire clock_1_out, clock_2_out, comparator_1_eq, decoder_1_out4, decoder_1_out5, decoder_2_out14, not_1_out,
       not_2_out, or_1_out, or_2_out, or_3_out;
  wire [3:0] adder_1_out, register_2_q;
  wire [11:0] controlled_buffer_2_out;
  wire [63:0] controlled_buffer_1_out, multiplexer_1_out, multiplexer_2_out, register_1_q;

  Decoder #(.select(4)) decoder_1 (
    .out4(decoder_1_out4), .out5(decoder_1_out5), .sel(icode));  // open: out0, out1, out2, out3, out6, out7, out8, out9, out10, out11, out12, out13, out14, out15, en
  or or_1 (or_1_out, decoder_1_out4, decoder_1_out5);
  Register #(.width(64)) register_1 (.D(valE), .clk(clock_1_out), .Q(register_1_q));  // open: en, clr
  Clock clock_1 (.out(clock_1_out));
  Multiplexer #(.width(64)) multiplexer_1 (.in0(register_1_q), .in1(valA), .out(multiplexer_1_out), .sel(not_1_out));
  not not_1 (not_1_out, or_2_out);
  or or_2 (or_2_out, decoder_1_out4, decoder_1_out5);
  or or_3 (or_3_out, decoder_1_out4, decoder_1_out5);
  not not_2 (not_2_out, or_3_out);
  assign controlled_buffer_1_out = or_1_out ? multiplexer_2_out : 64'bz;  // Controlled_Buffer controlled_buffer_1
  Multiplexer #(.width(64)) multiplexer_2 (.in0(valA), .in1(valP), .out(multiplexer_2_out), .sel(not_2_out));
  assign controlled_buffer_2_out = or_1_out ? multiplexer_1_out[11:0] : 12'bz;  // Controlled_Buffer controlled_buffer_2
  RAM #(.addrWidth(12), .dataWidth(64), .enables("line")) ram_1 (
    .addr(controlled_buffer_2_out), .we(decoder_1_out4), .oe(decoder_1_out5), .clk(clk),
    .din(controlled_buffer_1_out), .dout(valM));
  Register #(.width(4)) register_2 (
    .D(adder_1_out), .clk(clock_2_out), .Q(register_2_q), .clr(decoder_2_out14));  // open: en
  Adder #(.width(4)) adder_1 (.a(register_2_q), .b(4'b0001), .out(adder_1_out));  // open: cin, cout
  Clock clock_2 (.out(clock_2_out));
  Decoder #(.select(4)) decoder_2 (
    .out14(decoder_2_out14), .sel(register_2_q));  // open: out0, out1, out2, out3, out4, out5, out6, out7, out8, out9, out10, out11, out12, out13, out15, en
  Comparator #(.width(4)) comparator_1 (.a(4'b1101), .b(register_2_q), .eq(comparator_1_eq));  // open: gt, lt
endmodule

module intmem2 (
  input  [11:0] PC,
  input  clock,
  output [7:0] byte0,
  output [7:0] byte1,
  output [7:0] byte2,
  output [7:0] byte3,
  output [7:0] byte4,
  output [7:0] byte5,
  output [7:0] byte6,
  output [7:0] byte7,
  output [7:0] byte8,
  output [7:0] byte9
);

  wire decoder_1_out0, decoder_1_out1, decoder_1_out2, decoder_1_out3, decoder_1_out4, decoder_1_out5,
       decoder_1_out6, decoder_1_out7, decoder_1_out8, decoder_1_out9, decoder_1_out14;
  wire [7:0] rom_1_data;
  wire [11:0] adder_1_out, adder_2_out, register_1_q;

  Adder #(.width(12)) adder_1 (.a(register_1_q), .b(12'h1), .out(adder_1_out));  // open: cin, cout
  Register #(.width(12)) register_1 (
    .D(adder_1_out), .clk(clock), .Q(register_1_q), .clr(decoder_1_out14));  // open: en
  Adder #(.width(12)) adder_2 (.a(register_1_q), .b(PC), .out(adder_2_out));  // open: cin, cout
  ROM #(.addrWidth(12)) rom_1 (.addr(adder_2_out), .data(rom_1_data));
  Decoder #(.select(4)) decoder_1 (
    .out0(decoder_1_out0), .out1(decoder_1_out1), .out2(decoder_1_out2), .out3(decoder_1_out3),
    .out4(decoder_1_out4), .out5(decoder_1_out5), .out6(decoder_1_out6), .out7(decoder_1_out7),
    .out8(decoder_1_out8), .out9(decoder_1_out9), .out14(decoder_1_out14), .sel(register_1_q[3:0]));  // open: out10, out11, out12, out13, out15, en
  Register register_2 (.D(rom_1_data), .en(decoder_1_out0), .clk(clock), .Q(byte0));  // open: clr
  Register register_3 (.D(rom_1_data), .en(decoder_1_out1), .clk(clock), .Q(byte1));  // open: clr
  Register register_4 (.D(rom_1_data), .en(decoder_1_out2), .clk(clock), .Q(byte2));  // open: clr
  Register register_5 (.D(rom_1_data), .en(decoder_1_out3), .clk(clock), .Q(byte3));  // open: clr
  Register register_6 (.D(rom_1_data), .en(decoder_1_out4), .clk(clock), .Q(byte4));  // open: clr
  Register register_7 (.D(rom_1_data), .en(decoder_1_out5), .clk(clock), .Q(byte5));  // open: clr
  Register register_8 (.D(rom_1_data), .en(decoder_1_out6), .clk(clock), .Q(byte6));  // open: clr
  Register register_9 (.D(rom_1_data), .en(decoder_1_out7), .clk(clock), .Q(byte7));  // open: clr
  Register register_10 (.D(rom_1_data), .en(decoder_1_out8), .clk(clock), .Q(byte8));  // open: clr
  Register register_11 (.D(rom_1_data), .en(decoder_1_out9), .clk(clock), .Q(byte9));  // open: clr

  // Notes on the sheet:
  //   contents of rom_1 (hex, n*v repeats v):
  //   30 fa 1 7*0 30 fb 0 1 6*0 60 ab 40 ab 8*0 70 2a 8*0 10 50 cb
endmodule
